// Logisim project TinyCPU-FetchDecode.circ as structural Verilog: 1 circuit, main circuit FetchDecode
module FetchDecode (
  input  DEC_JUMP_NOT_ZERO,
  input  NOT_ZERO,
  input  CLK,
  input  RESET,
  input  DEC_HALT_ERROR,
  input  [15:0] PROGRAM_LIMIT,
  output JUMP_NOT_ZERO,
  output HALT_ERROR,
  output [11:0] PC_OUT,
  output [21:0] OPCODE
);

  wire COMPARATOR_430_190_gt;
  wire [15:0] ADDER_490_280_out;
  wire [15:12] PC_q;

  Register #(.width(16)) PC (.D(ADDER_490_280_out), .en(1'b1), .clk(CLK), .Q({PC_q, PC_OUT}), .clr(RESET));
  Comparator #(.width(16)) COMPARATOR_430_190 (
    .a(PROGRAM_LIMIT), .b({PC_q, PC_OUT}), .gt(COMPARATOR_430_190_gt));  // open: eq, lt
  Adder #(.width(16)) ADDER_490_280 (.a({PC_q, PC_OUT}), .b({16{1'b1}}), .out(ADDER_490_280_out));  // open: cin, cout
  ROM #(.addrWidth(12), .dataWidth(22)) INSTRUCTION_ROM (.addr(PC_OUT), .data(OPCODE));
  and JNZ_TAKEN (JUMP_NOT_ZERO, DEC_JUMP_NOT_ZERO, NOT_ZERO);
  or ERROR_HALT (HALT_ERROR, COMPARATOR_430_190_gt, DEC_HALT_ERROR);

  // Notes on the sheet:
  //   PROGRAM_LIMIT: initial=0xfff
  //   AP 7 machine format v1: stable six-bit opcode allocation and encoder-generated ROM
  //   contents of INSTRUCTION_ROM (hex, n*v repeats v):
  //   ffff 1c0065 3 1c0064 2a0000 50065 1c0064 240004 2c0000
endmodule
